// Logisim project counter.circ as structural Verilog: 1 circuit, main circuit main
module main (
  input  x,
  output _0,
  output _1,
  output _2,
  output _3
);

  wire _0_q, _1_q, _2_q, _3_q, clock_1_out;

  Clock clock_1 (.out(clock_1_out));
  J_K_Flip_Flop u__0 (.J(x), .clk(clock_1_out), .K(x), .Q(_0_q));  // open: Qn, preset, en, reset
  J_K_Flip_Flop u__1 (.clk(clock_1_out), .Q(_1_q));  // open: J, K, Qn, preset, en, reset
  J_K_Flip_Flop u__2 (.clk(clock_1_out), .Q(_2_q));  // open: J, K, Qn, preset, en, reset
  J_K_Flip_Flop u__3 (.clk(clock_1_out), .Q(_3_q));  // open: J, K, Qn, preset, en, reset
endmodule
